# Fritzing sketch eggculator_schematic (saved by Fritzing 0.9.3b)
breadboards: 1

parts:
  Bauteil1 = Arduino Uno (Rev3) - ICSP
  Bauteil2 = LCD1602-I2C
  R1 = Resistor [tolerance=±5% resistance=4.7k package=THT]
  S1 = Pushbutton [package="[THT]"]
  S2 = Pushbutton [package="[THT]"]
  S3 = Pushbutton [package="[THT]"]
  DS1 = DS18B20 1-Wire Temperature Sensor [part_number=DS18B20]

nets (from the schematic view):
  N1: Bauteil1.A4/SDA, Bauteil2.SDA
  N2: Bauteil1.A5/SCL, Bauteil2.SCL
  N3: Bauteil1.D8, R1.Pin_1, DS1.DQ
  N4: Bauteil1.D5_PWM, S3.Pin_1, S3.Pin_2
  N5: Bauteil1.D6_PWM, S2.Pin_1, S2.Pin_2
  N6: Bauteil1.D7, S1.Pin_1, S1.Pin_2
  5V: Bauteil1.5V, Bauteil2.VCC, R1.Pin_0, DS1.VDD
  GND: Bauteil1.GND, Bauteil2.GND, S1.Pin_3, S1.Pin_4, S2.Pin_3, S2.Pin_4, S3.Pin_3, S3.Pin_4, DS1.GND

custom parts:
  LCD1602-I2C: A standard character display, usually with 2x16 characters. Comes in many colors with LCM1602 IIC attached.
